// Digital circuit alu.dig as structural Verilog
module alu (
  input  [3:0] Op,
  input  [15:0] TData,
  input  [15:0] AData,
  output [15:0] RData
);

  wire [15:0] add_1_s, sub_1_s;

  Add #(.Bits(16)) add_1 (.a(TData), .b(AData), .c_i(1'b0), .s(add_1_s));  // open: c_o
  Sub #(.Bits(16)) sub_1 (.a(TData), .b(AData), .c_i(1'b0), .s(sub_1_s));  // open: c_o
  Multiplexer #(.Bits(16), .Selector_Bits(4)) multiplexer_1 (
    .sel(Op), .in_0(add_1_s), .in_1(sub_1_s), .in_2(AData), .in_3({16{1'b0}}), .in_4({16{1'b0}}),
    .in_5({16{1'b0}}), .in_6({16{1'b0}}), .in_7({16{1'b0}}), .in_8({16{1'b0}}), .in_9({16{1'b0}}),
    .in_10({16{1'b0}}), .in_11({16{1'b0}}), .in_12({16{1'b0}}), .in_13({16{1'b0}}), .in_14({16{1'b0}}),
    .in_15({16{1'b0}}), .out(RData));

  // Notes on the sheet:
  //   Op: Select which operation to perform 
  //   0x0 : Add
  //   0x1 : Subtract
  //   0x2 : Multiply
  //   0x3 : Divide
  //   TData: Data of the target operand
  //   AData: Data of the argument
  //   RData: Result data
endmodule
