// Digital circuit control.dig as structural Verilog
module control (
  input  [15:0] Instr,
  input  En,
  output [3:0] RT,
  output RTW,
  output [3:0] RA,
  output [3:0] AluOp,
  output AluD,
  output [7:0] Imm,
  output LoD,
  output HiD,
  output Jmp,
  output [3:0] JT,
  output Halt,
  output JReg,
  output RReg,
  output MemD,
  output RTD,
  output WMem,
  output WPC,
  output SPA,
  output MSP,
  output SPD,
  output DtoPC,
  output [1:0] PA,
  output PtoD,
  output PFtoD,
  output PW
);

  wire _0_3RA, _0_7Imm, _4_7RT, _4_15AllHigh, _8_11AluOp, _8_11Imm, _8_11JT, _8_11RT, _10_11PA, and_1_out,
       and_2_out, and_3_out, and_4_out, and_5_out, and_6_out, and_7_out, and_8_out, and_10_out, and_11_out,
       and_12_out, and_13_out, and_15_out, and_37_out, and_38_out, and_39_out, decoder_2_out_0,
       decoder_2_out_4, decoder_2_out_5, decoder_2_out_6, decoder_2_out_7, DtoPC_t, Halt_t, HiD_t, Jmp_t,
       JReg_t, LoD_t, MemD_t, MSP_t, or_3_out, or_4_out, or_11_out, PFtoD_t, PtoD_t, PW_t, RReg_t, RTD_t,
       RTW_t, SPA_t, SPD_t, WMem_t, WPC_t;
  wire [1:0] PA_t;
  wire [3:0] AluOp_t, JT_t, multiplexer_1_out, RA_t, RT_t;
  wire [7:0] Imm_t;

  and and_1 (and_1_out, Instr[8], ~Instr[9], ~Instr[10], ~Instr[11]);  // And
  and and_2 (and_2_out, and_3_out, and_1_out);
  and and_3 (and_3_out, ~Instr[12], ~Instr[13], ~Instr[14], ~Instr[15]);  // And
  and and_4 (and_4_out, and_2_out, ~Instr[0]);  // And
  and and_5 (and_5_out, and_2_out, Instr[0]);
  and and_6 (and_6_out, ~Instr[8], ~Instr[9], ~Instr[10], ~Instr[11]);  // And
  and and_7 (and_7_out, ~Instr[4], ~Instr[5], ~Instr[6], ~Instr[7]);  // And
  and and_8 (and_8_out, and_7_out, and_6_out, and_3_out);
  Multiplexer #(.Bits(4)) multiplexer_1 (.sel(and_8_out), .in_0(4'b0000), .in_1(Instr[3:0]), .out(multiplexer_1_out));
  Decoder #(.Selector_Bits(4)) decoder_1 (
    .sel(multiplexer_1_out), .out_1(DtoPC_t));  // open: out_0, out_2, out_3, out_4, out_5, out_6, out_7, out_8, out_9, out_10, out_11, out_12, out_13, out_14, out_15
  assign PA_t = _10_11PA ? Instr[11:10] : 2'bz;  // Driver driver_1
  assign JT_t = _8_11JT ? Instr[11:8] : 4'bz;  // Driver driver_2
  assign AluOp_t = _8_11AluOp ? Instr[11:8] : 4'bz;  // Driver driver_3
  assign RT_t = _8_11RT ? Instr[11:8] : 4'bz;  // Driver driver_4
  assign Imm_t = _8_11Imm ? {4'b0000, Instr[11:8]} : 8'bz;  // Driver driver_5
  Decoder #(.Selector_Bits(4)) decoder_2 (
    .sel(Instr[15:12]), .out_0(decoder_2_out_0), .out_1(_8_11AluOp), .out_2(LoD_t), .out_3(HiD_t),
    .out_4(decoder_2_out_4), .out_5(decoder_2_out_5), .out_6(decoder_2_out_6), .out_7(decoder_2_out_7),
    .out_8(WPC_t), .out_9(_10_11PA));  // open: out_10, out_11, out_12, out_13, out_14, out_15
  or or_1 (_8_11RT, LoD_t, HiD_t);
  or or_2 (_4_7RT, _8_11AluOp, decoder_2_out_6, decoder_2_out_7, _10_11PA, and_2_out);
  or or_3 (or_3_out, _8_11AluOp, LoD_t, HiD_t, decoder_2_out_6, _10_11PA);
  or or_4 (or_4_out, _8_11AluOp, decoder_2_out_5, decoder_2_out_6, decoder_2_out_7, WPC_t);
  or or_5 (_0_7Imm, LoD_t, HiD_t, decoder_2_out_4, WPC_t);
  or or_6 (Jmp_t, decoder_2_out_4, decoder_2_out_5, WPC_t, DtoPC_t);
  or or_7 (_8_11JT, decoder_2_out_4, decoder_2_out_5);
  and and_9 (Halt_t, decoder_2_out_0, _4_15AllHigh);
  and and_10 (and_10_out, WPC_t, Instr[11]);
  and and_11 (and_11_out, decoder_2_out_5, Instr[4]);
  and and_12 (and_12_out, WPC_t, Instr[8]);
  or or_8 (_8_11Imm, decoder_2_out_6, decoder_2_out_7);
  or or_9 (MemD_t, decoder_2_out_6, DtoPC_t, and_5_out);
  or or_10 (WMem_t, decoder_2_out_7, WPC_t, and_4_out);
  or or_11 (or_11_out, WPC_t, DtoPC_t);
  or or_12 (SPA_t, WPC_t, DtoPC_t, and_2_out);
  or or_13 (MSP_t, WPC_t, and_2_out, DtoPC_t);
  or or_14 (SPD_t, DtoPC_t, and_5_out);
  and and_13 (and_13_out, _10_11PA, Instr[8]);
  and and_14 (PW_t, _10_11PA, ~Instr[8]);  // And
  assign RT_t = _4_7RT ? Instr[7:4] : 4'bz;  // Driver driver_6
  or or_15 (RTW_t, or_3_out, and_5_out);
  or or_16 (_0_3RA, or_4_out, _10_11PA);
  or or_17 (JReg_t, decoder_2_out_5, and_10_out, DtoPC_t);
  or or_18 (RReg_t, and_11_out, and_12_out);
  and and_15 (and_15_out, _10_11PA, ~Instr[8]);  // And
  or or_19 (RTD_t, decoder_2_out_7, and_4_out, and_15_out);
  assign JT_t = or_11_out ? 4'b1111 : 4'bz;  // Driver driver_7
  and and_16 (PFtoD_t, and_13_out, Instr[9]);
  and and_17 (PtoD_t, and_13_out, ~Instr[9]);  // And
  assign Imm_t = _0_7Imm ? Instr[7:0] : 8'bz;  // Driver driver_8
  assign RA_t = _0_3RA ? Instr[3:0] : 4'bz;  // Driver driver_9
  and and_18 (RTW, RTW_t, En);
  and and_19 (AluD, _8_11AluOp, En);
  and and_20 (LoD, LoD_t, En);
  and and_21 (HiD, HiD_t, En);
  and and_22 (Jmp, Jmp_t, En);
  and and_23 (Halt, Halt_t, En);
  and and_24 (JReg, JReg_t, En);
  and and_25 (RReg, RReg_t, En);
  and and_26 (MemD, MemD_t, En);
  and and_27 (RTD, RTD_t, En);
  and and_28 (WMem, WMem_t, En);
  and and_29 (WPC, WPC_t, En);
  and and_30 (SPA, SPA_t, En);
  and and_31 (MSP, MSP_t, En);
  and and_32 (SPD, SPD_t, En);
  and and_33 (DtoPC, DtoPC_t, En);
  and and_34 (PtoD, PtoD_t, En);
  and and_35 (PFtoD, PFtoD_t, En);
  and and_36 (PW, PW_t, En);
  and and_37 (and_37_out, Instr[11], Instr[10]);
  and and_38 (and_38_out, Instr[9], Instr[8], Instr[7], Instr[6], Instr[5]);
  and and_39 (and_39_out, Instr[4], Instr[3], Instr[2], Instr[1], Instr[0]);
  assign RT = En ? RT_t : 4'bz;  // Driver driver_10
  assign RA = En ? RA_t : 4'bz;  // Driver driver_11
  assign AluOp = En ? AluOp_t : 4'bz;  // Driver driver_12
  assign Imm = En ? Imm_t : 8'bz;  // Driver driver_13
  assign JT = En ? JT_t : 4'bz;  // Driver driver_14
  assign PA = En ? PA_t : 2'bz;  // Driver driver_15
  and and_40 (_4_15AllHigh, and_37_out, and_38_out, and_39_out);

  // Other names for the same wires on the sheet: AluD_t = _8_11AluOp; b0 = Instr[0]; b4 = Instr[4]; b8 = Instr[8];
  //   b9 = Instr[9]; b11 = Instr[11]

  // Notes on the sheet:
  //   RT: Address of target register
  //   RTW: Address of target register
  //   RA: Address of argument register
  //   AluOp: ALU operation to perform
  //   En: Enabled when on
  //   AluD: High when ALU result should be sent to data bus
  //   Imm: 8 bit immediate value
  //   LoD: Write target with low bits set to Imm to data
  //   HiD: Write target with high bits set to Imm to data
  //   Jmp: When high, jump if jump decider is true
  //   JT: Four bit jump type
  //   Halt: When high, write jump location to data bus
  //   JReg: Jump using register based jump
  //   RReg: When jumping with a register, use it as a relative value
  //   MemD: When high, write memroy data to the data bus
  //   RTD: When high, write target register data to the data bus
  //   WMem: When high, write data from the data bus to memory
  //   WPC: When high, send the PC to memory instead of the data bus
  //   SPA: When high, use the stack pointer as the address intead of the computed address
  //   MSP: When high, modify the stack pointer
  //   SPD: When high, decrement and use a pre-decremented address
  //   DtoPC: When high, write the data bus to the jumpCalc register value instead of the argument register
  //   PA: Two bit peripheral address
  //   PtoD: When high, write data from the selected peripheral to data
  //   PFtoD: When high, write flags from the selected peripheral to data
  //   PW: When high, write data to the selected peripheral from data
  //   Noop
endmodule
