// Digital circuit hardware.dig as structural Verilog
module hardware (
  input  clk,
  input  in_2,
  input  in_3,
  input  [15:0] in_4,
  input  in_5,
  input  in_6
);

  wire AluD, and_1_out, and_2_out, DtoPC, Halt, HiD, Jmp, JReg, jumpdecider_1_djmp, LoD, MemD, MSP,
       not_1_out, Phase_out, RReg, rs_ff_1_nq, rs_ff_1_q, RTD, RTW, SPA, SPD, Un_Halt_out, WMem, WPC;
  wire [3:0] alu_1_fl, AluOp, JT, RA, RT;
  wire [7:0] addrcalc_1_p1;
  wire [15:0] add_1_s, addrcalc_1_p2, addrcalc_1_p3, counterpreset_1_out, driver_1_out, InstrReg_q,
       jumpcalc_1_npc, multiplexer_1_out, multiplexer_2_out, multiplexer_3_out, multiplexer_4_out,
       multiplexer_5_out, PC_out, ramdualport_1_d, registerfile_1_da, sub_1_s;

  RS_FF rs_ff_1 (.S(Halt), .C(clk), .R(Un_Halt_out), .Q(rs_ff_1_q), .nQ(rs_ff_1_nq));
  Button Un_Halt (.out(Un_Halt_out));
  and and_1 (and_1_out, rs_ff_1_nq, clk);
  Counter Phase (.en(1'b1), .C(and_1_out), .clr(1'b0), .out(Phase_out));  // open: ovf
  LED Halted (.in(rs_ff_1_q));
  LED Running (.in(and_1_out));
  not not_1 (not_1_out, Phase_out);
  and and_2 (and_2_out, MSP, Phase_out);
  CounterPreset #(.Bits(16)) counterpreset_1 (
    .en(and_2_out), .C(and_1_out), .dir(SPD), .in(in_4), .ld(in_5), .clr(in_6), .out(counterpreset_1_out));  // open: ovf
  Add #(.Bits(16)) add_1 (.a(counterpreset_1_out), .b(16'h8000), .c_i(1'b0), .s(add_1_s));  // open: c_o
  Sub #(.Bits(16)) sub_1 (.a(add_1_s), .b(16'h1), .c_i(1'b0), .s(sub_1_s));  // open: c_o
  Multiplexer #(.Bits(16)) multiplexer_1 (
    .sel(DtoPC), .in_0(addrcalc_1_p2), .in_1(driver_1_out), .out(multiplexer_1_out));
  jumpCalc jumpcalc_1 (
    .PC(PC_out), .Imm(addrcalc_1_p1), .Reg(multiplexer_1_out), .JReg(JReg), .RRel(RReg), .nPC(jumpcalc_1_npc));
  jumpDecider jumpdecider_1 (.Jmp(Jmp), .JT(JT), .Fl(alu_1_fl), .DJmp(jumpdecider_1_djmp));
  Multiplexer #(.Bits(16)) multiplexer_2 (.sel(SPD), .in_0(add_1_s), .in_1(sub_1_s), .out(multiplexer_2_out));
  // Probe on jumpcalc_1_npc
  CounterPreset #(.Bits(16)) PC (
    .en(not_1_out), .C(and_1_out), .dir(in_2), .in(jumpcalc_1_npc), .ld(jumpdecider_1_djmp), .clr(in_3),
    .out(PC_out));  // open: ovf
  // addrCalc addrcalc_1: pin names not known; wires that end beside it: addrcalc_1_p1, addrcalc_1_p2, addrcalc_1_p3
  Multiplexer #(.Bits(16)) multiplexer_3 (
    .sel(SPA), .in_0(addrcalc_1_p3), .in_1(multiplexer_2_out), .out(multiplexer_3_out));
  Multiplexer #(.Bits(16)) multiplexer_4 (
    .sel(Phase_out), .in_0(PC_out), .in_1(multiplexer_3_out), .out(multiplexer_4_out));
  Multiplexer #(.Bits(16)) multiplexer_5 (.sel(WPC), .in_0(driver_1_out), .in_1(PC_out), .out(multiplexer_5_out));
  RegisterFile #(.AddrBits(4), .Bits(16)) registerfile_1 (
    .Din(driver_1_out), .we(RTW), .Rw(RT), .C(and_1_out), .Ra(RT), .Rb(RA), .Da(registerfile_1_da),
    .Db(addrcalc_1_p2));
  RAMDualPort #(.AddrBits(16), .isProgramMemory("true"), .Bits(16)) ramdualport_1 (
    .A(multiplexer_4_out), .Din(multiplexer_5_out), .str(WMem), .C(and_1_out), .ld(1'b1), .D(ramdualport_1_d));
  assign driver_1_out = RTD ? registerfile_1_da : 16'bz;  // Driver driver_1
  assign driver_1_out = MemD ? ramdualport_1_d : 16'bz;  // Driver driver_2
  Register #(.Bits(16)) InstrReg (.D(ramdualport_1_d), .C(and_1_out), .en(not_1_out), .Q(InstrReg_q));
  alu alu_1 (
    .Op(AluOp), .TData(registerfile_1_da), .AData(addrcalc_1_p2), .DO(AluD), .Clk(and_1_out),
    .RData(driver_1_out), .Fl(alu_1_fl));
  // Probe on InstrReg_q
  control control_1 (
    .Instr(InstrReg_q), .En(Phase_out), .RT(RT), .RTW(RTW), .RA(RA), .AluOp(AluOp), .AluD(AluD),
    .Imm(addrcalc_1_p1), .LoD(LoD), .HiD(HiD), .Jmp(Jmp), .JT(JT), .Halt(Halt), .JReg(JReg), .RReg(RReg),
    .MemD(MemD), .RTD(RTD), .WMem(WMem), .WPC(WPC), .SPA(SPA), .MSP(MSP), .SPD(SPD), .DtoPC(DtoPC));  // open: PA, PtoD, PFtoD, PW, SPtoD, SPSub, SPL, SPLImm
  overwriter overwriter_1 (.Data(addrcalc_1_p1), .Lo(LoD), .Hi(HiD), .Val(registerfile_1_da), .ValU(driver_1_out));
  // Probe on addrcalc_1_p1
  // Probe on driver_1_out
  LED led_1 (.in(alu_1_fl[0]));
  LED led_2 (.in(alu_1_fl[1]));
  LED led_3 (.in(alu_1_fl[2]));
  LED led_4 (.in(alu_1_fl[3]));

  // Notes on the sheet:
  //   clk: Hz: 20
  //   Imm
  //   Data
  //   fN
  //   fZ
  //   fC
  //   fO
endmodule
